# Fritzing sketch sonar3 (saved by Fritzing 0.9.10b)
breadboards: 1

parts:
  부품1 = Arduino Mega 2560 (Rev3)
  HC-SR04_Sensor_1 = HC-SR04 Ultrasonic Distance Sensor
  S1 = H-Bridge with L298N  # not connected
  HC-SR04_Sensor_2 = HC-SR04 Ultrasonic Distance Sensor
  HC-SR04_Sensor_3 = HC-SR04 Ultrasonic Distance Sensor

nets:
  VCC: 부품1.5V, HC-SR04_Sensor_1.VCC, HC-SR04_Sensor_2.VCC, HC-SR04_Sensor_3.VCC
  GND: 부품1.GND, HC-SR04_Sensor_1.GND, HC-SR04_Sensor_2.GND, HC-SR04_Sensor_3.GND
  N1: 부품1.D3_PWM, HC-SR04_Sensor_1.TRIG
  N2: 부품1.D4_PWM, HC-SR04_Sensor_1.ECHO

custom parts:
  H-Bridge with L298N: h-bridge
